// Logisim project LookAheadAdder.circ as structural Verilog: 1 circuit, main circuit main
module main (
  input  X3,
  input  X2,
  input  X1,
  input  X0,
  input  Y2,
  input  Y1,
  input  Y0,
  input  Y3,
  input  c0,
  output S3,
  output S2,
  output S1,
  output S0,
  output C4
);

  wire and_1_out, and_2_out, and_3_out, and_4_out, and_5_out, and_6_out, and_7_out, and_8_out, and_9_out,
       and_10_out, and_11_out, and_12_out, and_13_out, and_14_out, or_1_out, or_2_out, or_4_out, xor_1_out,
       xor_2_out, xor_3_out, xor_4_out;

  xor xor_1 (xor_1_out, X1, Y1);
  and and_1 (and_1_out, X1, Y1);
  xor xor_2 (xor_2_out, X2, Y2);
  and and_2 (and_2_out, X2, Y2);
  xor xor_3 (xor_3_out, X3, Y3);
  and and_3 (and_3_out, X3, Y3);
  xor xor_4 (xor_4_out, X0, Y0);
  and and_4 (and_4_out, X0, Y0);
  xor xor_5 (S2, xor_2_out, or_2_out);
  xor xor_6 (S0, xor_4_out, c0);
  xor xor_7 (S1, xor_1_out, or_1_out);
  and and_5 (and_5_out, c0, xor_4_out);
  and and_6 (and_6_out, xor_3_out, and_2_out);
  and and_7 (and_7_out, xor_3_out, xor_2_out, and_1_out);
  and and_8 (and_8_out, xor_3_out, xor_2_out, xor_1_out, and_4_out);
  and and_9 (and_9_out, xor_3_out, xor_2_out, xor_1_out, xor_4_out, c0);
  or or_1 (or_1_out, and_5_out, and_4_out);
  and and_10 (and_10_out, and_4_out, xor_1_out);
  and and_11 (and_11_out, xor_4_out, xor_1_out, c0);
  and and_12 (and_12_out, xor_2_out, and_1_out);
  and and_13 (and_13_out, xor_1_out, xor_2_out, and_4_out);
  and and_14 (and_14_out, xor_1_out, xor_4_out, xor_2_out, c0);
  or or_2 (or_2_out, and_10_out, and_1_out, and_11_out);
  xor xor_8 (S3, xor_3_out, or_4_out);
  or or_3 (C4, and_3_out, and_6_out, and_7_out, and_8_out, and_9_out);
  or or_4 (or_4_out, and_2_out, and_12_out, and_13_out, and_14_out);

  // Notes on the sheet:
  //   P1
  //   G1
  //   P2
  //   G2
  //   P3
  //   G3
  //   P0
  //   G0
  //   C1
  //   C2
  //   C3
endmodule
